# Fritzing sketch Clock_wired (saved by Fritzing 0.9.3b)
breadboards: 1

parts:
  Part1 = Arduino Uno (Rev3)
  S1 = Pushbutton [package="[SMD]"]
  S2 = Pushbutton [package="[SMD]"]
  J1 = Piezo Speaker
  LED1 = smd LED [color="Blue (505nm)" package="1206 [SMD]"]
  R1 = Resistor [tolerance=±5% resistance=10k package="0805 [SMD]"]
  R2 = Resistor [tolerance=±5% resistance=220 package="1206 [SMD]"]
  LED2 = smd LED [color="Red (635nm)" package="1206 [SMD]"]
  R3 = Resistor [tolerance=±5% resistance=220 package="1206 [SMD]"]
  R4 = Resistor [tolerance=±5% resistance=10k package="0805 [SMD]"]
  LED3 = smd LED [color="Green (570nm)" package="1206 [SMD]"]
  LED4 = smd LED [color="Yellow (585nm)" package="1206 [SMD]"]
  LED5 = smd LED [color="Red (635nm)" package="1206 [SMD]"]
  R5 = Resistor [tolerance=±5% resistance=220 package="1206 [SMD]"]
  R6 = Resistor [tolerance=±5% resistance=220 package="1206 [SMD]"]
  R7 = Resistor [tolerance=±5% resistance=220 package="1206 [SMD]"]

nets:
  N1: Part1.D10_PWM/SS, R3.Pin_1
  N2: Part1.D11_PWM/MOSI, S2.Pin_1, S2.Pin_2, R4.Pin_0
  N3: Part1.D12/MISO, R2.Pin_1
  N4: Part1.D13/SCK, S1.Pin_1, S1.Pin_2, R1.Pin_0
  N5: Part1.D2, J1.pin2
  N6: Part1.D4, R7.Pin_1
  N7: Part1.D6_PWM, R6.Pin_1
  N8: Part1.D7, R5.Pin_1
  N9: Part1.5V, S1.Pin_3, S1.Pin_4, S2.Pin_3, S2.Pin_4
  N10: Part1.GND, J1.pin1, LED1.cathode, R1.Pin_1, LED2.cathode, R4.Pin_1, LED3.cathode, LED4.cathode, LED5.cathode
  N11: LED1.anode, R2.Pin_0
  N12: LED2.anode, R3.Pin_0
  N13: LED3.anode, R5.Pin_0
  N14: LED4.anode, R6.Pin_0
  N15: LED5.anode, R7.Pin_0
